# Fritzing sketch Compte-pose (saved by Fritzing 0.9.3b)
circuit board: 8.46667cm x 5.64444cm
breadboards: 1

parts:
  RE2 = Rotary Encoder [package=THT]
  C1 = [richard] Capacitor 100nF [capacitance=100nF voltage=35V package="7.5mm [THT, pp]"]
  C2 = [richard] Capacitor 100nF [capacitance=100nF voltage=35V package="7.5mm [THT, pp]"]
  Composant1 = Arduino Uno (Rev3) - ICSP
  R1 = Resistor [tolerance=±5% resistance=100 package=THT]
  R2 = Resistor [tolerance=±5% resistance=100 package=THT]
  J1 = shrouded pin header, 16 pins [form="♂ (shrouded male)"]
  J2 = double row rounded female pin header, 16 pins [form="♀ (female rounded)"]

nets:
  N1: RE2.EncoderPinA, R1.Pin_1
  N2: RE2.EncoderPinC, C1.-, C2.-, J1.pin2
  N3: RE2.EncoderPinB, R2.Pin_1
  N4: C1.+, R1.Pin_0, J1.pin4
  N5: C2.+, R2.Pin_0, J1.pin3
  N6: Composant1.GND, J2.pin15
  N7: Composant1.D2, J2.pin14
  N8: Composant1.D3_PWM, J2.pin13
  N9: Composant1.3V3, J2.pin16

custom parts:
  [richard] Capacitor 100nF: Polypropylene/Film and Foil capacitor.
